# Fritzing sketch Bedini Autotuner Testbed_recover (saved by Fritzing 0.7.7b)
breadboards: 4

parts:
  S1 = Pushbutton [package="[THT]"]
  LCD1 = LCD screen
  S2 = Pushbutton [package="[THT]"]
  Auto_ON_LED = LED - 5mm [color="Green (570nm)" package="5 mm [THT]"]
  Manual_LED = LED - 5mm [color="Red (633nm)" package="5 mm [THT]"]
  Part1 = Thumb Joystick
  R1 = Resistor [tolerance=±5% resistance=220 package=THT]
  IR_LED = LED - 5mm [color="Infrared (940nm)" package="5 mm [THT]"]
  R2 = Resistor [tolerance=±5% resistance=330 package=THT]
  D1 = Rectifier Diode [part_number=1N4004 package="300 mil [THT]"]
  Arduino_SLAVE = Arduino
  D2 = Rectifier Diode [part_number=1N4004 package="300 mil [THT]"]
  R3 = Resistor [tolerance=±5% resistance=330 package=THT]
  COIL_Junction_Box = screw terminal, 8 pins
  Arduino_MASTER = Arduino
  IR_Receiver = LED - 5mm [color="Infrared (940nm)" package="5 mm [THT]"]
  R4 = Resistor [tolerance=±5% resistance=330 package=THT]
  CHG_Battery_Bank = 4 x AAA Battery Mount
  SRC_Battery_Bank = 4 x AAA Battery Mount
  H11D1_-_1 = Optocoupler [package=THT]
  Q1 = Basic FET N-Channel [package="TO220 [THT]"]
  L1 = Inductor [package="400 mil [THT]"]  # not connected
  Pad1 = Pad [width=7.90222222222222 height=9.03111111111111 connect=center]  # not connected
  Pad2 = Pad [width=7.90222222222222 height=9.03111111111111 connect=center]  # not connected

nets (from the schematic view):
  GND: S1.Pin_1, S1.Pin_2, S1.Pin_3, S1.Pin_4, LCD1.V0, S2.Pin_1, S2.Pin_2, S2.Pin_3, S2.Pin_4, Auto_ON_LED.anode, Manual_LED.anode, Part1.GND, Part1.SEL, IR_LED.anode, Arduino_SLAVE.GND, COIL_Junction_Box.pin1, Arduino_MASTER.D13, Arduino_MASTER.D12, Arduino_MASTER.A1, IR_Receiver.anode
  VDD: LCD1.VDD, Part1.VCC, R1.Pin_0, Arduino_SLAVE.VIN, Arduino_MASTER.+5V, Arduino_MASTER.A0
  N1: LCD1.R/W, Arduino_MASTER.D8
  N2: Auto_ON_LED.cathode, Arduino_MASTER.D11
  N3: Manual_LED.cathode, Arduino_MASTER.D10
  N4: R2.Pin_0, H11D1_-_1.Pin_2
  N5: D1.cathode, H11D1_-_1.Pin_4, Q1.gate
  N6: D1.anode, SRC_Battery_Bank.-, Q1.source
  N7: Arduino_SLAVE.D13, H11D1_-_1.Pin_1
  N8: Arduino_SLAVE.D7, Arduino_MASTER.D6
  N9: Arduino_SLAVE.D6, Arduino_MASTER.D7
  N10: Arduino_SLAVE.A0, R4.Pin_1
  N11: D2.cathode, CHG_Battery_Bank.+
  N12: D2.anode, COIL_Junction_Box.pin3, Q1.drain
  N13: R3.Pin_0, CHG_Battery_Bank.-, SRC_Battery_Bank.+
  N14: R3.Pin_1, H11D1_-_1.Pin_5
  N15: COIL_Junction_Box.pin2, R4.Pin_0

notes:
  SRC Bar
  CHG Bar
  Optical Tachometer
